# Fritzing sketch TVOut_Demo_Circuit (saved by Fritzing 0.8.7b)
breadboards: 1

parts:
  Part1 = Arduino Mega 2560 (Rev3)
  JP1 = RCA [package=rca]  # not connected
  R1 = Resistor [tolerance=±5% resistance=470 package=THT]
  R2 = Resistor [tolerance=±10% resistance=1k package=THT]
  R3 = Resistor [tolerance=±5% resistance=100 package=THT]
  SP1 = SPEAKER [part_number="8ohm, 0.5W" package=pcb_mount_speaker]

nets:
  N1: Part1.D11_PWM, R2.Pin_1
  N2: Part1.D10_PWM, R3.Pin_1
  N3: Part1.GND, SP1.+
  N4: Part1.D29, R1.Pin_1
  N5: R1.Pin_0, R2.Pin_0
  N6: R3.Pin_0, SP1.-
